# Fritzing sketch frizling_schematics_M8kF26dafQ (saved by Fritzing 0.9.3b)
breadboards: 1

parts:
  Part1 = Arduino MKR1000
  Part2 = Logic Level Converter
  Part3 = OBD II UART
  LCD1 = LCD screen
  R1 = Trimmer Potentiometer [maximum_resistance=10kΩ package=THT]
  R2 = Resistor [tolerance=±5% resistance=220 package="0805 [SMD]"]

nets:
  N1: Part1.D2_PWM, LCD1.DB7
  N2: Part1.D3_PWM, LCD1.DB6
  N3: Part1.D4_PWM, LCD1.DB5
  N4: Part1.D5_PWM, LCD1.DB4
  N5: Part1.D11_SDA, LCD1.E
  N6: Part1.D12_SCL, LCD1.RS
  N7: Part1.D13_RX, Part2.TX_LV
  N8: Part1.14_TX, Part2.RX_LV
  GND: Part1.GND, Part2.GND, Part3.GND, LCD1.VSS, LCD1.R/W, LCD1.LED-, R1.leg1
  N9: Part1.VCC, Part2.LV
  5V: Part1.5V, Part2.HV, LCD1.VDD, R1.leg2, R2.Pin_0
  N10: Part2.TX_HV, Part3.TX-O
  N11: Part2.RX_HV, Part3.RX-I
  N12: LCD1.V0, R1.wiper
  N13: LCD1.LED+, R2.Pin_1

custom parts:
  Arduino MKR1000: MKR1000 is a powerful board that combines the functionality of the Zero and the Wi-Fi Shield. It is the ideal solution for makers wanting to design IoT projects with minimal previous experience in networking
